# Fritzing sketch Diagrama conexiones - Wifi Car (saved by Fritzing 0.9.3b)

parts:
  VCC1 = 4 x AAA Battery Mount
  Part1 = Adafruit FeatherWing Doubler [part_number="Adafruit #2890"]
  Part2 = Adafruit DC+Stepper FeatherWing [part_number="Adafruit #2927"]
  Part3 = Adafruit Feather HUZZAH ESP8266 [part_number="Adafruit #2821"]
  M1 = DC Motor
  M2 = DC Motor

nets:
  GND: VCC1.-, Part1.GND, Part2.GND, Part3.GND
  N1: VCC1.+, Part2.VMOTOR
  N2: Part1.G, Part2.G, Part3.CH_PD
  N3: Part1.TX, Part2.TX, Part3.TXD
  N4: Part1.MOSI, Part1.M, Part2.MOSI, Part2.L, Part3.GPIO13/MOSI
  N5: Part1.F, Part2.F
  +3.3V: Part1.3V, Part2.+3.3V, Part3.3.3V
  N6: Part1.RX, Part2.RX, Part3.RXD
  N7: Part1.A, Part2.A, Part3.ADC
  N8: Part1.RESET, Part2.RESET, Part3.RESET
  N9: Part1.AREF, Part2.AREF
  N10: Part1.C, Part2.C
  N11: Part1.SCK, Part1.O, Part2.SCK, Part2.N, Part3.GPIO14/SCK
  N12: Part1.MISO, Part1.N, Part2.M, Part2.MISO, Part3.GPIO12/MISO
  N13: Part1.SDA, Part2.SDA, Part3.GPIO4/SDA
  N14: Part1.SCL, Part2.SCL, Part3.GPIO5/SCL
  N15: Part1.J, Part2.I, Part3.GPIO16
  N16: Part1.I, Part2.H, Part3.GPIO2
  N17: Part1.K, Part2.J, Part3.GPIO0
  N18: Part1.L, Part2.K, Part3.GPIO15
  N19: Part1.USB, Part2.USB, Part3.VBUS
  N20: Part1.EN, Part2.EN, Part3.EN
  N21: Part1.VBAT, Part2.VBAT, Part3.VBAT
  N22: Part1.B, Part2.B
  N23: Part1.D, Part2.D
  N24: Part1.E, Part2.E
  N25: Part2.M1B, M2.pin_1
  N26: Part2.M1A, M2.pin_2
  N27: Part2.M4A, M1.pin_1
  N28: Part2.M4B, M1.pin_2

custom parts:
  Adafruit FeatherWing Doubler: This is the FeatherWing Doubler - a prototyping add-on and more for all Feather boards. This is similar to our FeatherWing Proto except there are two! The magic of the Doubler comes when stacking a Feather and another board on top of the Doubler so you can work with both boards simultaneously side-by-side! The Doubler, like the Proto, has a duplicate breakout for each pin on a Feather, as well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
  Adafruit DC+Stepper FeatherWing: This is the DC Motor + Stepper FeatherWing which will let you use 2 x bi-polar stepper motors or 4 x brushed DC motorx (or 1 stepper and 2 DC motors). Using our Feather Stacking Headers or Feather Female Headers you can connect a FeatherWing on top or bottom of your Feather board and let the board take flight! The original Adafruit Motorshield Kit is one of our most beloved kits, which is why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
  Adafruit Feather HUZZAH ESP8266: his is the Adafruit Feather HUZZAH ESP8266 - our take on an 'all-in-one' ESP8266 WiFi development board with built in USB and battery charging. Its an ESP8266 WiFi module with all the extras you need, ready to rock! We have other boards in the Feather family, check'em out here. At the Feather HUZZAH's heart is an ESP8266 WiFi microcontroller clocked at 80 MHz and at 3.3V logic. This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
